// Digital circuit XOR3_new.dig as structural Verilog
module XOR3_new (
  input  A,
  input  B,
  input  C,
  output Q
);

  wire and_1_out, and_2_out, and_3_out, and_4_out, not_1_out, not_2_out, not_3_out, not_4_out, or_1_out;

  not not_1 (not_1_out, A);
  not not_2 (not_2_out, B);
  not not_3 (not_3_out, C);
  and and_1 (and_1_out, A, not_2_out);
  and and_2 (and_2_out, not_1_out, B);
  or or_1 (or_1_out, and_1_out, and_2_out);
  not not_4 (not_4_out, or_1_out);
  and and_3 (and_3_out, C, not_4_out);
  and and_4 (and_4_out, not_3_out, or_1_out);
  or or_2 (Q, and_3_out, and_4_out);
endmodule
