// Digital circuit bubble3.dig as structural Verilog
module bubble3 (
  input  A,
  input  B,
  input  C,
  input  D,
  input  E,
  output Y
);

  wire and_1_out, and_2_out, not_1_out, not_2_out, or_1_out;

  not not_1 (not_1_out, D);
  and and_1 (and_1_out, A, not_2_out);
  not not_2 (not_2_out, B);
  or or_1 (or_1_out, not_1_out, E);
  and and_2 (and_2_out, and_1_out, C);
  or or_2 (Y, and_2_out, or_1_out);
endmodule
