// Digital circuit kmap-1.dig as structural Verilog
module kmap_1 (
  input  B,
  input  C,
  output Y
);

  wire not_1_out;

  not not_1 (not_1_out, B);
  or or_1 (Y, not_1_out, C);

  // Notes on the sheet:
  //   Y: Y
endmodule
