// Digital circuit kmap-2.dig as structural Verilog
module kmap_2 (
  input  C,
  input  D,
  input  B,
  input  A,
  output Y
);

  wire and_1_out, and_2_out, not_1_out, or_1_out;

  and and_1 (and_1_out, A, D);
  and and_2 (and_2_out, not_1_out, D);
  not not_1 (not_1_out, C);
  or or_1 (or_1_out, and_1_out, and_2_out);
  or or_2 (Y, B, or_1_out);
endmodule
