// Digital circuit kmap2-3.dig as structural Verilog
module kmap2_3 (
  input  A,
  input  B,
  input  C,
  input  D,
  input  E,
  output Y
);

  wire and_1_out, and_2_out, and_3_out, not_1_out, not_2_out, not_3_out;

  not not_1 (not_1_out, A);
  not not_2 (not_2_out, C);
  not not_3 (not_3_out, D);
  and and_1 (and_1_out, not_1_out, B, not_2_out, D);
  and and_2 (and_2_out, A, B, C, D);
  and and_3 (and_3_out, B, not_3_out, E);
  or or_1 (Y, and_1_out, and_2_out, and_3_out);
endmodule
