// Digital circuit SR-latch.dig as structural Verilog
module SR_latch (
  input  R,
  input  S,
  output Q,
  output Qb
);

  nor nor_1 (Q, R, Qb);
  nor nor_2 (Qb, Q, S);
endmodule

/* Test case:
R S Q Qb
0 0 1 0
1 0 0 1
1 1 0 0
1 0 0 1
0 0 0 1
*/
