// Digital circuit fair_coffee_machine.dig as structural Verilog
module fair_coffee_machine (
  input  clk
);

  wire and_1_out, and_2_out, and_3_out, and_4_out, and_5_out, and_6_out, and_7_out, and_8_out, and_9_out,
       Coin_out, Large_Coffee_out, not_1_out, not_2_out, not_3_out, or_1_out, or_2_out, or_3_out, or_4_out,
       S_0_nq, S_0_q, S_1_nq, S_1_q, Small_Coffee_out;

  Button Coin (.out(Coin_out));
  Button Small_Coffee (.out(Small_Coffee_out));
  not not_1 (not_1_out, Coin_out);
  not not_2 (not_2_out, Small_Coffee_out);
  Button Large_Coffee (.out(Large_Coffee_out));
  not not_3 (not_3_out, Large_Coffee_out);
  and and_1 (and_1_out, S_1_nq, S_0_nq, Coin_out);
  and and_2 (and_2_out, S_1_nq, S_0_q, not_1_out, not_2_out);
  and and_3 (and_3_out, S_1_q, S_0_nq, not_1_out, Small_Coffee_out, not_3_out);
  and and_4 (and_4_out, S_1_nq, S_0_q, Coin_out, not_2_out);
  and and_5 (and_5_out, S_1_q, S_0_nq, not_2_out, not_3_out);
  and and_6 (and_6_out, S_1_q, S_0_nq, Coin_out);
  and and_7 (and_7_out, S_1_nq, S_0_q, Small_Coffee_out);
  and and_8 (and_8_out, S_1_q, S_0_nq, Small_Coffee_out);
  and and_9 (and_9_out, S_1_q, S_0_nq, Large_Coffee_out);
  or or_1 (or_1_out, and_1_out, and_2_out, and_3_out);
  or or_2 (or_2_out, and_4_out, and_5_out);
  or or_3 (or_3_out, S_0_q, S_1_q);
  or or_4 (or_4_out, and_7_out, and_8_out);
  D_FF S_0 (.D(or_1_out), .C(clk), .Q(S_0_q), .nQ(S_0_nq));
  D_FF S_1 (.D(or_2_out), .C(clk), .Q(S_1_q), .nQ(S_1_nq));
  LED Ready (.in(or_3_out));
  LED Return_Coin (.in(and_6_out));
  LED Brew_Small_Coffee (.in(or_4_out));
  LED Brew_LARGE_Coffee (.in(and_9_out));
endmodule
